// Logisim project Project.circ as structural Verilog: 1 circuit, main circuit main
module main (
  input  S0,
  input  [3:0] X,
  input  [3:0] Y,
  input  [1:0] S2S1,
  input  S3,
  input  [3:0] X_2,
  input  [3:0] Y_2,
  input  S2,
  input  [1:0] S1S0,
  input  S3_2,
  input  IL,
  input  [1:0] S1S0_2,
  input  [3:0] X_3,
  input  [1:0] S1S0_3,
  input  [3:0] Y_3,
  input  [1:0] S1S0_4,
  input  [1:0] S1S0_5,
  output N,
  output Z,
  output C,
  output V,
  output [3:0] F
);

  wire and_2_out, not_3_out, not_4_out, not_5_out, not_6_out, xnor_1_out, xor_2_out;
  wire [3:0] adder_1_out, and_1_out, multiplexer_1_out, multiplexer_2_out, multiplexer_3_out,
       multiplexer_7_out, not_1_out, not_2_out, or_1_out, xor_1_out;

  assign not_1_out = ~Y;  // NOT_Gate not_1, 4 bits wide
  assign and_1_out = X_2 & Y_2;  // AND_Gate and_1, 4 bits wide
  assign xor_1_out = X_2 ^ Y_2;  // XOR_Gate xor_1, 4 bits wide
  assign or_1_out = X_2 | Y_2;  // OR_Gate or_1, 4 bits wide
  assign not_2_out = ~X_2;  // NOT_Gate not_2, 4 bits wide
  Multiplexer #(.select(2), .width(4)) multiplexer_1 (
    .in0(4'b0000), .in1(X), .in2(not_1_out), .in3(4'b1111), .out(multiplexer_1_out), .sel(S2S1));  // open: en
  not not_3 (not_3_out, Y_3[0]);
  not not_4 (not_4_out, Y_3[1]);
  not not_5 (not_5_out, Y_3[2]);
  not not_6 (not_6_out, Y_3[3]);
  Adder #(.width(4)) adder_1 (.a(X), .b(multiplexer_1_out), .out(adder_1_out), .cin(S0), .cout(C));
  Multiplexer #(.select(2), .width(4)) multiplexer_2 (
    .in0(and_1_out), .in1(xor_1_out), .in2(or_1_out), .in3(not_2_out), .out(multiplexer_2_out), .sel(S1S0));  // open: en
  Multiplexer #(.select(2)) multiplexer_3 (
    .in0(not_3_out), .in1(IL), .in2(Y_3[0]), .in3(Y_3[1]), .out(multiplexer_3_out[0]), .sel(S1S0_2));  // open: en
  Multiplexer #(.select(2)) multiplexer_4 (
    .in0(not_4_out), .in1(X_3[0]), .in2(Y_3[1]), .in3(Y_3[2]), .out(multiplexer_3_out[1]), .sel(S1S0_3));  // open: en
  Multiplexer #(.select(2)) multiplexer_5 (
    .in0(not_5_out), .in1(X_3[1]), .in2(X_3[1]), .in3(Y_3[3]), .out(multiplexer_3_out[2]), .sel(S1S0_4));  // open: en
  Multiplexer #(.select(2)) multiplexer_6 (
    .in0(not_6_out), .in1(X_3[2]), .in2(Y_3[3]), .in3(Y_3[0]), .out(multiplexer_3_out[3]), .sel(S1S0_5));  // open: en
  Multiplexer #(.width(4)) multiplexer_7 (
    .in0(adder_1_out), .in1(multiplexer_2_out), .out(multiplexer_7_out), .sel(S3));  // open: en
  nor nor_1 (Z, F[3], F[2], F[1], F[0]);
  Multiplexer #(.width(4)) multiplexer_8 (
    .in0(multiplexer_7_out), .in1(multiplexer_3_out), .out(F), .sel(and_2_out));  // open: en
  and and_2 (and_2_out, S2, S3_2);
  xnor xnor_1 (xnor_1_out, X[3], multiplexer_1_out[3]);
  xor xor_2 (xor_2_out, multiplexer_1_out[3], adder_1_out[3]);
  and and_3 (V, xnor_1_out, xor_2_out);

  assign N = F[3];

  // Notes on the sheet:
  //   Yara Altwaijry
  //   438201218
endmodule
